# Fritzing sketch arduino-nano-touch (saved by Fritzing 1.0.1rc)
circuit board: 5.71332cm x 5.6024cm
breadboards: 1

parts:
  U4 = 3.5mm Audio Jack [package=audio-jack]
  U5 = 3.5mm Audio Jack [package=audio-jack]
  U6 = 3.5mm Audio Jack [package=audio-jack]
  Nano1 = Arduino Nano v2.3
  R1 = Resistor [tolerance=±5% power=0.25 resistance=100 package=THT]
  R2 = Resistor [tolerance=±5% power=0.25 resistance=100 package=THT]
  R3 = Resistor [tolerance=±5% power=0.25 resistance=100 package=THT]

nets:
  touch1: U4.RIGHT, U4.LEFT, R3.Pin_1
  N1: U4.SLEEVE, U5.SLEEVE, U6.SLEEVE
  touch2: U5.RIGHT, U5.LEFT, R2.Pin_1
  touch3: U6.RIGHT, U6.LEFT, R1.Pin_1
  N2: Nano1.D2, R3.Pin_0
  N3: Nano1.D3, R2.Pin_0
  N4: Nano1.D4, R1.Pin_0
  GND: Nano1.GND
