# Fritzing sketch esp32-s3 touch-v2 (saved by Fritzing 1.0.1rc)
circuit board: 8.26666cm x 5.3825cm
breadboards: 1

parts:
  M1 = ESP32-S3-DevKitC-1-N8R8-v1 [part_number=ESP32-S3-DevKitC-1-N8R8-v1]
  J1 = female pin header, 12 pins [form="♀ (female)"]
  J2 = female pin header, 12 pins [form="♀ (female)"]
  GND_5V = female pin header, 2 pins [form="♀ (female)"]
  J4 = female pin header, 2 pins [form="♀ (female)"]
  J5 = female pin header, 2 pins [form="♀ (female)"]

nets:
  N1: M1.pin_4, J1.pin12
  N2: M1.pin_5, J1.pin11
  N3: M1.pin_6, J1.pin10
  N4: M1.pin_7, J1.pin9
  N5: M1.pin_12, J1.pin8
  N6: M1.pin_13, J1.pin7
  N7: M1.pin_15, J1.pin6
  N8: M1.pin_16, J1.pin5
  N9: M1.pin_17, J1.pin4
  N10: M1.pin_18, J1.pin3
  N11: M1.pin_19, J1.pin2
  N12: M1.pin_20, J1.pin1
  N13: M1.pin_21, GND_5V.pin2
  GND: M1.pin_22, M1.pin_23, M1.pin_24, M1.pin_44, J2.pin1, J2.pin2, J2.pin3, J2.pin4, J2.pin5, J2.pin6, J2.pin7, J2.pin8, J2.pin9, J2.pin10, J2.pin11, J2.pin12, GND_5V.pin1, J5.pin1, J5.pin2
  N14: M1.pin_40, J4.pin2
  N15: M1.pin_41, J4.pin1

notes:
  Touch sensor
  ESP32-S3 WROOM-1-N16R8
  ESP32-S3-DevKitC-1
  4
  5
  6
  7
  3
  8
  11
  12
  10
  9
  13
  14
  1
  2

custom parts:
  ESP32-S3-DevKitC-1-N8R8-v1: ESP32-S3-DevKitC-1-N8R8-v1 This module is 44pins long (2x22) and 11 pins width.
