# Fritzing sketch esp32-s3 touch (saved by Fritzing 1.0.1rc)
circuit board: 8.68999cm x 5.85287cm
breadboards: 1

parts:
  M1 = ESP32-S3-DevKitC-1-N8R8-v1 [part_number=ESP32-S3-DevKitC-1-N8R8-v1]
  Pad1 = Pad [width=7.902222222222222 height=9.03111111111111 connect=center]
  Pad2 = Pad [width=7.902222222222222 height=9.03111111111111 connect=center]
  Pad3 = Pad [width=7.902222222222222 height=9.03111111111111 connect=center]
  Pad4 = Pad [width=7.902222222222222 height=9.03111111111111 connect=center]
  Pad5 = Pad [width=7.902222222222222 height=9.03111111111111 connect=center]
  Pad6 = Pad [width=7.902222222222222 height=9.03111111111111 connect=center]
  Pad7 = Pad [width=7.902222222222222 height=9.03111111111111 connect=center]
  Pad8 = Pad [width=7.902222222222222 height=9.03111111111111 connect=center]
  J1 = female pin header, 8 pins [form="♀ (female)"]
  J2 = female pin header, 6 pins [form="♀ (female)"]

nets:
  N1: M1.pin_4, J2.pin4
  N2: M1.pin_5, J2.pin3
  N3: M1.pin_6, J2.pin2
  N4: M1.pin_7, J2.pin1
  N5: M1.pin_12, Pad8.pad, J1.pin8
  N6: M1.pin_13, Pad7.pad, J1.pin7
  N7: M1.pin_15, Pad6.pad, J1.pin6
  N8: M1.pin_16, Pad5.pad, J1.pin5
  N9: M1.pin_17, Pad4.pad, J1.pin4
  N10: M1.pin_18, Pad3.pad, J1.pin3
  N11: M1.pin_19, Pad2.pad, J1.pin2
  N12: M1.pin_20, Pad1.pad, J1.pin1
  N13: M1.pin_40, J2.pin5
  N14: M1.pin_41, J2.pin6

notes:
  touch sensor
  N2048 @ January 2026

custom parts:
  ESP32-S3-DevKitC-1-N8R8-v1: ESP32-S3-DevKitC-1-N8R8-v1 This module is 44pins long (2x22) and 11 pins width.
